# Fritzing sketch LED Light Sensor (saved by Fritzing 0.7.1b)

parts:
  U1 = Arduino Mega
  LED1 = LED - 5mm [color="Red (633nm)" package="5 mm [THT]"]
  LED2 = LED - 5mm [color="Red (633nm)" package="5 mm [THT]"]

nets:
  N1: U1.GND, LED1.cathode, LED2.cathode
  N2: U1.D13, LED1.anode
  N3: U1.A0, LED2.anode
