# Fritzing sketch Synth 1 (saved by Fritzing 0.7.1b)
breadboards: 1

parts:
  Arduino1 = Arduino
  U1 = 4093

nets:
  +5V: Arduino1.+5V, U1.VDD
  GND: Arduino1.GND, U1.VSS
  N1: U1.1A, U1.1B

custom parts:
  4093: Quad 2-input NAND Schmitt trigger
