# Fritzing sketch Synth 2 (saved by Fritzing 0.7.1b)
breadboards: 1

parts:
  Arduino1 = Arduino
  U1 = 4093
  Frequency = Rotary Potentiometer (Small) [maximum_resistance=100kΩ]
  Volume = Rotary Potentiometer (Small) [maximum_resistance=10kΩ]
  C1 = Electrolytic Capacitor [package="100 mil [THT, electrolytic]"]
  IC1 = DIP - 8 pins [package="DIP (Dual Inline) [THT]"]
  SPKR1 = Loudspeaker
  C3 = Electrolytic Capacitor [package="100 mil [THT, electrolytic]"]

nets:
  GND: Arduino1.GND, U1.VSS, Volume.leg2, C1.-, IC1.-INPUT, SPKR1.pin1
  +5V: Arduino1.+5V, U1.VDD, IC1.V_S
  N1: U1.1A, U1.1B, Frequency.leg1, C1.+
  N2: U1.1Y, Frequency.wiper, Volume.leg1
  N3: Volume.wiper, IC1.+INPUT
  N4: IC1.V_OUT, C3.+
  N5: SPKR1.pin2, C3.-

custom parts:
  4093: Quad 2-input NAND Schmitt trigger
  Electrolytic Capacitor: A small electrolytic capacitor
  DIP - 8 pins: A DIP stand-in part for whatever IC you want. With 8 pins on a 300 mil dual inline package (DIP) footprint.
  Electrolytic Capacitor: A small electrolytic capacitor
